# Fritzing sketch quadro de chamada (saved by Fritzing 1.0.5)

parts:
  ESP_32_Wroom = DOIT Esp32 DevKit v1 (30 pins long, 11 pins width) [part_number=ESP32S-PIN30]
  Relá_1_e_2 = 2-Channel 5v Relay Shield [package=relay-2ch5v10a]
  Relé_3_e_4 = 2-Channel 5v Relay Shield [package=relay-2ch5v10a]
  DHT11 = Humidity and Temperature Sensor DHT11
  Botão_Mute = Round Pushbutton
  Terra = Multimeter straight black probe
  S6 = Taiway 100-SP-X-T1 SPDT Miniature Toggle Switch [part_number=100-SP-X-T1-0-0-B1-M1 package=THT]
  S7 = Taiway 100-SP-X-T1 SPDT Miniature Toggle Switch [part_number=100-SP-X-T1-0-0-B1-M1 package=THT]
  S8 = Taiway 100-SP-X-T1 SPDT Miniature Toggle Switch [part_number=100-SP-X-T1-0-0-B1-M1 package=THT]
  S9 = Taiway 100-SP-X-T1 SPDT Miniature Toggle Switch [part_number=100-SP-X-T1-0-0-B1-M1 package=THT]
  VCC_3_3V = Multimeter straight red probe
  VCC_5_0V = Multimeter straight red probe
  LM117 = Voltage Regulator [package=to220-adj]
  LED1 = LED - 3mm [color="Red (633nm)" current=0.030A package="3 mm [THT]"]
  Arandela_de_Led_127V = LED - 3mm [color="Red (633nm)" current=0.030A package="3 mm [THT]"]
  LED3 = LED - 3mm [color="Red (633nm)" current=0.030A package="3 mm [THT]"]
  LED4 = LED - 3mm [color="Red (633nm)" current=0.030A package="3 mm [THT]"]
  Buzzer = Piezo Speaker
  Fase_127VCA-Neutro-Terra = Camdenboss CTB0158-3 [part_number=CTB0158-3 package=THT]

nets:
  N1: ESP_32_Wroom.3V3, DHT11.GND_2
  N2: ESP_32_Wroom.GND, DHT11.Data-signal, Terra.Probe_meter_end, LM117.ADJ
  N3: ESP_32_Wroom.D15, DHT11.Vcc
  N4: ESP_32_Wroom.D4, Relá_1_e_2.IN2
  N5: ESP_32_Wroom.D5, Relá_1_e_2.IN1
  N6: ESP_32_Wroom.D18, Relé_3_e_4.IN2
  N7: ESP_32_Wroom.D19, Relé_3_e_4.IN1
  N8: ESP_32_Wroom.D21, Buzzer.pin2
  N9: ESP_32_Wroom.D32, S6.L1
  N10: ESP_32_Wroom.D33, S7.L1
  N11: ESP_32_Wroom.D25, S8.L1
  N12: ESP_32_Wroom.D26, S9.L1
  N13: ESP_32_Wroom.D27, Botão_Mute.leg1
  N14: ESP_32_Wroom.VIN, VCC_5_0V.Probe_meter_end, VCC_5_0V.Probe_tip_2
  N15: Relá_1_e_2.K1-Off, LED4.cathode
  N16: Relá_1_e_2.K2-Off, LED3.cathode
  N17: Relé_3_e_4.K1-Off, Arandela_de_Led_127V.cathode
  N18: Relé_3_e_4.K2-In, Fase_127VCA-Neutro-Terra.terminal_1
  N19: Relé_3_e_4.K2-Off, LED1.cathode
  N20: VCC_3_3V.Probe_meter_end, LM117.OUT
  N21: Arandela_de_Led_127V.anode, Fase_127VCA-Neutro-Terra.terminal_2

custom parts:
  DOIT Esp32 DevKit v1 (30 pins long, 11 pins width): The DOIT Esp32 DevKit v1 is one of the development board created by DOIT to evaluate the ESP-WROOM-32 module. It is based on the ESP32 microcontroller that boasts Wifi, Bluetooth, Ethernet and Low Power support all in a single chip. (vanepp) made breadboard work, adjusted pin numbering and labels and reduced size of schematic and cleaned up pcb. This chip is 30pins long (2 x15) and 11 pins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
  2-Channel 5v Relay Shield: 2 Channel 5v Relay Shield w. 2x SPD-06VDC-SD-C
  Humidity and Temperature Sensor DHT11: Digital relative humidity & temperature sensor DHT11
